// Digital circuit Template.dig as structural Verilog
module Template (
  input  A,
  input  B,
  input  Cin,
  output Sum,
  output Cout
);

  wire and_1_out, and_2_out, and_3_out, and_4_out, and_5_out, and_6_out, and_7_out, and_8_out, and_9_out,
       and_10_out, and_11_out, and_12_out, and_13_out, and_14_out, and_15_out, and_16_out, not_1_out,
       not_2_out, not_3_out, not_4_out, not_5_out, not_6_out, not_7_out, not_8_out, not_9_out;

  not not_1 (not_1_out, A);
  not not_2 (not_2_out, B);
  not not_3 (not_3_out, A);
  not not_4 (not_4_out, Cin);
  not not_5 (not_5_out, B);
  not not_6 (not_6_out, Cin);
  not not_7 (not_7_out, A);
  not not_8 (not_8_out, B);
  not not_9 (not_9_out, Cin);
  and and_1 (and_1_out, not_1_out, not_2_out);
  and and_2 (and_2_out, not_3_out, B);
  and and_3 (and_3_out, A, not_5_out);
  and and_4 (and_4_out, A, B);
  and and_5 (and_5_out, not_7_out, B);
  and and_6 (and_6_out, A, not_8_out);
  and and_7 (and_7_out, A, B);
  and and_8 (and_8_out, A, B);
  and and_9 (and_9_out, and_1_out, Cin);
  and and_10 (and_10_out, and_2_out, not_4_out);
  and and_11 (and_11_out, and_3_out, not_6_out);
  and and_12 (and_12_out, and_4_out, Cin);
  and and_13 (and_13_out, and_5_out, Cin);
  and and_14 (and_14_out, and_6_out, Cin);
  and and_15 (and_15_out, and_7_out, not_9_out);
  and and_16 (and_16_out, and_8_out, Cin);
  or or_1 (Sum, and_9_out, and_10_out, and_11_out, and_12_out);
  or or_2 (Cout, and_13_out, and_14_out, and_15_out, and_16_out);
endmodule
