// Digital circuit Template.dig as structural Verilog
module Template (
  input  A,
  input  B,
  input  C,
  input  D,
  output Z1,
  output Z2,
  output Z3
);

  wire and_1_out, and_2_out, and_3_out, and_4_out, and_5_out, and_6_out, and_7_out, and_8_out, and_9_out,
       and_10_out, and_11_out, and_12_out, and_13_out, and_14_out, and_15_out, and_16_out, not_1_out,
       not_2_out, not_3_out, not_4_out, not_5_out, not_6_out, not_7_out, not_8_out, not_9_out, not_10_out,
       not_11_out, not_12_out, not_13_out, not_14_out, not_15_out, not_16_out, not_17_out, not_18_out,
       not_19_out, not_20_out, not_21_out, not_22_out, not_23_out, not_24_out, not_25_out, not_26_out,
       not_27_out, not_28_out, not_29_out, not_30_out, not_31_out, not_32_out;

  not not_1 (not_1_out, A);
  not not_2 (not_2_out, C);
  not not_3 (not_3_out, D);
  not not_4 (not_4_out, B);
  not not_5 (not_5_out, C);
  not not_6 (not_6_out, D);
  not not_7 (not_7_out, B);
  not not_8 (not_8_out, C);
  not not_9 (not_9_out, C);
  not not_10 (not_10_out, D);
  not not_11 (not_11_out, C);
  not not_12 (not_12_out, D);
  and and_1 (and_1_out, not_1_out, B, not_2_out, not_3_out);
  and and_2 (and_2_out, A, not_4_out, not_5_out, not_6_out);
  and and_3 (and_3_out, A, not_7_out, not_8_out, D);
  and and_4 (and_4_out, A, B, not_9_out, not_10_out);
  and and_5 (and_5_out, A, B, not_11_out, D);
  and and_6 (and_6_out, A, B, C, not_12_out);
  or or_1 (Z1, and_1_out, and_2_out, and_3_out, and_4_out, and_5_out, and_6_out);
  not not_13 (not_13_out, A);
  not not_14 (not_14_out, B);
  not not_15 (not_15_out, C);
  not not_16 (not_16_out, A);
  not not_17 (not_17_out, B);
  not not_18 (not_18_out, D);
  not not_19 (not_19_out, A);
  not not_20 (not_20_out, B);
  not not_21 (not_21_out, A);
  not not_22 (not_22_out, D);
  not not_23 (not_23_out, A);
  not not_24 (not_24_out, B);
  and and_7 (and_7_out, not_13_out, not_14_out, not_15_out, D);
  and and_8 (and_8_out, not_16_out, not_17_out, C, not_18_out);
  and and_9 (and_9_out, not_19_out, not_20_out, C, D);
  and and_10 (and_10_out, not_21_out, B, C, not_22_out);
  and and_11 (and_11_out, not_23_out, B, C, D);
  and and_12 (and_12_out, A, not_24_out, C, D);
  or or_2 (Z2, and_7_out, and_8_out, and_9_out, and_10_out, and_11_out, and_12_out);
  not not_25 (not_25_out, A);
  not not_26 (not_26_out, B);
  not not_27 (not_27_out, C);
  not not_28 (not_28_out, D);
  not not_29 (not_29_out, A);
  not not_30 (not_30_out, C);
  not not_31 (not_31_out, B);
  not not_32 (not_32_out, D);
  and and_13 (and_13_out, not_25_out, not_26_out, not_27_out, not_28_out);
  and and_14 (and_14_out, not_29_out, B, not_30_out, D);
  and and_15 (and_15_out, A, not_31_out, C, not_32_out);
  and and_16 (and_16_out, A, B, C, D);
  or or_3 (Z3, and_13_out, and_14_out, and_15_out, and_16_out);
endmodule
