// Digital circuit Template-02.dig as structural Verilog
module Template_02 (
  input  [2:0] In,
  input  clk,
  output [7:0] Z
);

  wire and_1_out, and_2_out, and_3_out, and_4_out, and_5_out, and_6_out, and_7_out, and_8_out, and_9_out,
       and_10_out, and_11_out, not_1_out, not_2_out, not_3_out, not_4_out, not_5_out, not_6_out, not_7_out,
       not_8_out, not_9_out, not_10_out, not_11_out, not_12_out, not_13_out, not_14_out, not_15_out,
       not_16_out, not_17_out, not_18_out, not_19_out, not_20_out, not_21_out, not_22_out, not_23_out,
       not_24_out, not_25_out, not_26_out, not_27_out, or_1_out, or_2_out, or_3_out, or_4_out, or_5_out,
       or_6_out;

  or or_1 (or_1_out, In[2], In[1], In[0]);
  or or_2 (or_2_out, In[2], not_1_out, not_2_out);
  not not_1 (not_1_out, In[1]);
  not not_2 (not_2_out, In[0]);
  or or_3 (or_3_out, not_3_out, In[1], not_4_out);
  not not_3 (not_3_out, In[2]);
  not not_4 (not_4_out, In[0]);
  and and_1 (and_1_out, not_5_out, not_6_out, In[0]);
  not not_5 (not_5_out, In[2]);
  not not_6 (not_6_out, In[1]);
  and and_2 (and_2_out, not_7_out, In[1], In[0]);
  not not_7 (not_7_out, In[2]);
  and and_3 (and_3_out, In[2], not_8_out, not_9_out);
  not not_8 (not_8_out, In[1]);
  not not_9 (not_9_out, In[0]);
  and and_4 (and_4_out, In[2], not_10_out, In[0]);
  not not_10 (not_10_out, In[1]);
  or or_4 (or_4_out, In[2], In[1], not_11_out);
  not not_11 (not_11_out, In[0]);
  or or_5 (or_5_out, not_12_out, not_13_out, In[0]);
  not not_12 (not_12_out, In[2]);
  not not_13 (not_13_out, In[1]);
  or or_6 (or_6_out, not_14_out, not_15_out, not_16_out);
  not not_14 (not_14_out, In[2]);
  not not_15 (not_15_out, In[1]);
  not not_16 (not_16_out, In[0]);
  and and_5 (and_5_out, not_17_out, In[1], not_18_out);
  not not_17 (not_17_out, In[2]);
  not not_18 (not_18_out, In[0]);
  and and_6 (and_6_out, In[2], not_19_out, not_20_out);
  not not_19 (not_19_out, In[1]);
  not not_20 (not_20_out, In[0]);
  and and_7 (and_7_out, In[2], In[1], In[0]);
  and and_8 (and_8_out, not_21_out, not_22_out, In[0]);
  not not_21 (not_21_out, In[2]);
  not not_22 (not_22_out, In[1]);
  and and_9 (and_9_out, not_23_out, In[1], not_24_out);
  not not_23 (not_23_out, In[2]);
  not not_24 (not_24_out, In[0]);
  and and_10 (and_10_out, In[2], not_25_out, not_26_out);
  not not_25 (not_25_out, In[1]);
  not not_26 (not_26_out, In[0]);
  and and_11 (and_11_out, In[2], In[1], not_27_out);
  not not_27 (not_27_out, In[0]);
  and and_12 (Z[5], or_1_out, or_2_out, or_3_out);
  or or_7 (Z[3], and_1_out, and_2_out, and_3_out, and_4_out);
  and and_13 (Z[2], or_4_out, or_5_out, or_6_out);
  or or_8 (Z[1], and_5_out, and_6_out, and_7_out);
  or or_9 (Z[0], and_8_out, and_9_out, and_10_out, and_11_out);
  Terminal terminal_1 (.D({2'b01, Z[5], 1'b0, Z[3:0]}), .C(clk), .en(1'b1));

  assign {Z[7:6], Z[4]} = 3'b010;
endmodule
