// Digital circuit 01.dig as structural Verilog
module _01 (
  input  [3:0] In,
  output A,
  output B,
  output C,
  output D,
  output E,
  output F,
  output G
);

  wire In0_t, In1__In0, In1_t, In2__In0, In2__In0_t, In2__In1, In2_In1, In2_In1__In0, In2_In1_In0,
       In2_In1_In0_t, In2_t;

  not not_1 (In0_t, In[0]);
  not not_2 (In1_t, In[1]);
  not not_3 (In2_t, In[2]);
  and and_1 (In2_In1, In[2], In1_t);
  and and_2 (In2__In0, In2_t, In[0]);
  and and_3 (In1__In0, In1_t, In0_t);
  and and_4 (In2_In1_In0, In[2], In[1], In[0]);
  and and_5 (In2__In1, In2_t, In[1]);
  and and_6 (In2_In1__In0, In[2], In1_t, In[0]);
  and and_7 (In2__In0_t, In2_t, In0_t);
  and and_8 (In2_In1_In0_t, In[2], In[1], In0_t);
  or or_1 (A, In2_In1_In0, In2__In1, In2_In1__In0, In2__In0_t, In2_In1_In0_t, In[3]);
  or or_2 (B, In2__In0, In1__In0, In2_In1_In0, In2__In0_t);
  or or_3 (C, In2__In0, In1__In0, In2_In1_In0, In2_In1__In0, In2_In1_In0_t);
  or or_4 (D, In2__In1, In2_In1__In0, In2__In0_t, In2_In1_In0_t, In[3]);
  or or_5 (E, In2__In0_t, In2_In1_In0_t);
  or or_6 (F, In1__In0, In2_In1_In0, In2_In1__In0, In2_In1_In0_t, In[3]);
  or or_7 (G, In2_In1, In2__In1, In2_In1_In0_t, In[3]);
endmodule
