// Digital circuit 02.dig as structural Verilog
module _02 (
  input  [2:0] In,
  output [7:0] Z
);

  wire In0_t, In1__In0, In1_In0, In1_t, In2__In1__In0, In2__In1_In0, In2__In1_In0_t, In2_In1, In2_In1__In0,
       In2_In1_In0, In2_t;

  not not_1 (In0_t, In[0]);
  not not_2 (In1_t, In[1]);
  not not_3 (In2_t, In[2]);
  and and_1 (In2__In1_In0_t, In2_t, In[1], In0_t);
  and and_2 (In2_In1__In0, In[2], In1_t, In0_t);
  and and_3 (In2__In1_In0, In2_t, In[1], In[0]);
  and and_4 (In2_In1_In0, In[2], In[1], In[0]);
  and and_5 (In1__In0, In1_t, In0_t);
  and and_6 (In2__In1__In0, In2_t, In1_t, In[0]);
  and and_7 (In2_In1, In[2], In1_t);
  and and_8 (In1_In0, In[1], In0_t);
  or or_1 (Z[6], In2__In1_In0, In2_In1_In0, In1__In0, In2__In1__In0, In2_In1, In1_In0);
  or or_2 (Z[5], In2_In1__In0, In2_In1_In0, In2__In1__In0, In1_In0);
  or or_3 (Z[3], In2__In1_In0, In2__In1__In0, In2_In1);
  or or_4 (Z[2], In2__In1_In0_t, In2__In1_In0, In1__In0, In2_In1);
  or or_5 (Z[1], In2__In1_In0_t, In2_In1__In0, In2_In1_In0);
  or or_6 (Z[0], In2_In1__In0, In2__In1__In0, In1_In0);

  assign {Z[7], Z[4]} = 2'b00;
endmodule
