// Digital circuit 03.dig as structural Verilog
module _03 (
  input  [3:0] In,
  input  [1:0] Selector,
  output [3:0] Output
);

  wire In0_t, In1_t, In2_In1__In0, In2_t, S0__In2_In0, S0__In2_In1, S0_In1__In0, S0_In2_In1, S0_t,
       S1__In1_In0, S1__S0__In1__In0, S1__S0__In1_In0, S1__S0__In2__In0, S1__S0__In2__In1, S1__S0_In2__In1,
       S1__S0_In2_In1, S1__S0_In3, S1_In0, S1_In2_In1, S1_In2_In1__In0, S1_In3, S1_S0__In2__In1, S1_S0__In3,
       S1_S0_In1_In0, S1_S0_In1_In0_t, S1_S0_In2__In1__In0, S1_t;

  not not_1 (In0_t, In[0]);
  not not_2 (In1_t, In[1]);
  not not_3 (In2_t, In[2]);
  not not_4 (S0_t, Selector[0]);
  not not_5 (S1_t, Selector[1]);
  and and_1 (S1_S0_In2__In1__In0, Selector[1], Selector[0], In2_t, In1_t, In[0]);
  and and_2 (S1__S0__In2__In0, S1_t, S0_t, In2_t, In[0]);
  and and_3 (S1__S0__In1__In0, S1_t, S0_t, In1_t, In0_t);
  and and_4 (S1_S0_In1_In0_t, Selector[1], Selector[0], In[1], In0_t);
  and and_5 (S1__S0_In2__In1, S1_t, Selector[0], In2_t, In[1]);
  and and_6 (S1_S0_In1_In0, Selector[1], Selector[0], In[1], In[0]);
  and and_7 (S1__S0__In2__In1, S1_t, S0_t, In2_t, In[1]);
  and and_8 (S1_S0__In2__In1, Selector[1], S0_t, In2_t, In[1]);
  and and_9 (S1__S0__In1_In0, S1_t, S0_t, In[1], In[0]);
  and and_10 (S1_In2_In1__In0, Selector[1], In[2], In1_t, In[0]);
  and and_11 (S1__S0_In2_In1, S1_t, Selector[0], In[2], In1_t);
  and and_12 (In2_In1__In0, In[2], In1_t, In0_t);
  and and_13 (S1__In1_In0, S1_t, In[1], In0_t);
  and and_14 (S0_In1__In0, Selector[0], In1_t, In[0]);
  and and_15 (S0__In2_In0, S0_t, In[2], In[0]);
  and and_16 (S1__S0_In3, S1_t, Selector[0], In[3]);
  and and_17 (S0__In2_In1, S0_t, In[2], In[1]);
  and and_18 (S1_S0__In3, Selector[1], S0_t, In[3]);
  and and_19 (S0_In2_In1, Selector[0], In[2], In[1]);
  and and_20 (S1_In2_In1, Selector[1], In[2], In[1]);
  and and_21 (S1_In3, Selector[1], In[3]);
  and and_22 (S1_In0, Selector[1], In[0]);
  or or_1 (Output[3], S1_S0_In1_In0, S1_In2_In1__In0, S0__In2_In0, S0__In2_In1, In[3]);
  or or_2 (Output[2], S1_S0_In2__In1__In0, S1__S0__In2__In0, S1__S0__In2__In1, S1__S0_In2_In1, In2_In1__In0, S1__S0_In3, S1_S0__In3, S0_In2_In1, S1_In2_In1);
  or or_3 (Output[1], S1__S0__In1__In0, S1_S0_In1_In0_t, S1__S0_In2__In1, S1_S0__In2__In1, S1__S0__In1_In0, S1_In2_In1__In0, S1__S0_In2_In1, S1_In3);
  or or_4 (Output[0], S1__S0__In1__In0, S1__In1_In0, S0_In1__In0, S1_In0);

  // Other names for the same wires on the sheet: O0 = Output[0]; O1 = Output[1]; O2 = Output[2]; O3 = Output[3];
  //   S0 = Selector[0]; S1 = Selector[1]
endmodule
