// Digital circuit 04.dig as structural Verilog
module _04 (
  input  [6:0] In,
  output [6:0] Output
);

  wire In0_t, In1_t, In2_t, In3_t, In4_t, In5__In4__In1_In0, In5__In4__In3__In2__In1_In0, In5__In4__In3_In2,
       In5__In4__In3_In2_In1__In0, In5__In4_In3_In2__In1__In0, In5_In4__In1__In0, In5_In4__In1_In0,
       In5_In4__In3__In2, In5_In4__In3__In2_In1_In0, In5_In4__In3_In2, In5_In4__In3_In2__In1__In0,
       In5_In4_In3__In2__In1__In0, In5_t, In6__In4__In2_In0, In6__In4__In3__In2_In1__In0, In6__In4__In3_In1,
       In6__In4__In3_In2__In1_In0, In6__In4_In3_In2__In1__In0, In6__In5__In3_In2__In1__In0,
       In6__In5__In3_In2_In1_In0, In6__In5__In4__In2_In1_In0, In6__In5__In4__In3_In1_In0,
       In6__In5__In4__In3_In2_In0, In6__In5__In4__In3_In2_In1, In6__In5__In4_In2__In1__In0,
       In6__In5__In4_In3_In1__In0, In6__In5__In4_In3_In2__In0, In6__In5__In4_In3_In2__In1,
       In6__In5_In3__In2_In1__In0, In6__In5_In3_In2__In1_In0, In6__In5_In4__In2__In1_In0,
       In6__In5_In4__In3__In1__In0, In6__In5_In4__In3__In2_In1, In6__In5_In4__In3_In2__In0,
       In6_In4__In2__In0, In6_In4__In2_In0, In6_In4__In3__In1, In6_In4__In3__In2_In1_In0, In6_In4__In3_In1,
       In6_In4__In3_In2__In1__In0, In6_In4_In3__In2__In1__In0, In6_In5__In3__In2__In1_In0,
       In6_In5__In3_In2_In1__In0, In6_In5__In4__In2_In1__In0, In6_In5__In4__In3__In2__In0,
       In6_In5__In4__In3__In2__In1, In6_In5__In4__In3_In1__In0, In6_In5_In3__In2__In1__In0,
       In6_In5_In3__In2_In1_In0, In6_In5_In3_In2__In1__In0, In6_In5_In4__In2__In1__In0,
       In6_In5_In4__In3__In1_In0, In6_In5_In4__In3__In2_In0, In6_In5_In4__In3_In2__In1,
       In6_In5_In4_In2__In1__In0, In6_In5_In4_In3__In1__In0, In6_In5_In4_In3__In2__In0,
       In6_In5_In4_In3__In2__In1, In6_t;

  not not_1 (In0_t, In[0]);
  not not_2 (In1_t, In[1]);
  not not_3 (In2_t, In[2]);
  not not_4 (In3_t, In[3]);
  not not_5 (In4_t, In[4]);
  not not_6 (In5_t, In[5]);
  not not_7 (In6_t, In[6]);
  and and_1 (In6_In5_In4__In3__In1_In0, In[6], In[5], In4_t, In3_t, In[1], In0_t);
  and and_2 (In6__In5__In4__In3_In1_In0, In6_t, In5_t, In4_t, In[3], In[1], In[0]);
  and and_3 (In6_In5_In4__In3__In2_In0, In[6], In[5], In4_t, In3_t, In[2], In0_t);
  and and_4 (In6__In5__In4__In3_In2_In0, In6_t, In5_t, In4_t, In[3], In[2], In[0]);
  and and_5 (In5_In4__In3__In2_In1_In0, In[5], In4_t, In3_t, In[2], In[1], In0_t);
  and and_6 (In6_In4__In3__In2_In1_In0, In[6], In4_t, In3_t, In[2], In[1], In0_t);
  and and_7 (In6__In5__In4__In2_In1_In0, In6_t, In5_t, In4_t, In[2], In[1], In[0]);
  and and_8 (In6__In5__In4__In3_In2_In1, In6_t, In5_t, In4_t, In[3], In[2], In[1]);
  and and_9 (In6_In5__In4__In3_In1__In0, In[6], In5_t, In4_t, In[3], In1_t, In0_t);
  and and_10 (In6__In5_In4__In3__In1__In0, In6_t, In[5], In4_t, In3_t, In1_t, In[0]);
  and and_11 (In6__In5_In4__In3_In2__In0, In6_t, In[5], In4_t, In[3], In2_t, In0_t);
  and and_12 (In6_In5__In4__In3__In2__In0, In[6], In5_t, In4_t, In3_t, In2_t, In[0]);
  and and_13 (In5__In4__In3_In2_In1__In0, In5_t, In4_t, In[3], In[2], In1_t, In0_t);
  and and_14 (In5__In4__In3__In2__In1_In0, In5_t, In4_t, In3_t, In2_t, In[1], In[0]);
  and and_15 (In6__In4__In3_In2__In1_In0, In6_t, In4_t, In[3], In2_t, In[1], In0_t);
  and and_16 (In6__In4__In3__In2_In1__In0, In6_t, In4_t, In3_t, In[2], In1_t, In[0]);
  and and_17 (In6_In5__In4__In2_In1__In0, In[6], In5_t, In4_t, In[2], In1_t, In0_t);
  and and_18 (In6__In5_In4__In2__In1_In0, In6_t, In[5], In4_t, In2_t, In[1], In0_t);
  and and_19 (In6__In5_In4__In3__In2_In1, In6_t, In[5], In4_t, In3_t, In[2], In1_t);
  and and_20 (In6_In5__In4__In3__In2__In1, In[6], In5_t, In4_t, In3_t, In2_t, In[1]);
  and and_21 (In5_In4__In3_In2__In1__In0, In[5], In4_t, In[3], In2_t, In1_t, In[0]);
  and and_22 (In6_In4__In3_In2__In1__In0, In[6], In4_t, In[3], In2_t, In1_t, In[0]);
  and and_23 (In6_In5_In4_In3__In1__In0, In[6], In[5], In[4], In3_t, In1_t, In0_t);
  and and_24 (In6_In5_In4_In3__In2__In0, In[6], In[5], In[4], In3_t, In2_t, In0_t);
  and and_25 (In6_In5_In4__In2__In1__In0, In[6], In[5], In4_t, In2_t, In1_t, In[0]);
  and and_26 (In6_In5_In4__In3_In2__In1, In[6], In[5], In4_t, In[3], In2_t, In1_t);
  and and_27 (In6__In5__In4_In3_In1__In0, In6_t, In5_t, In[4], In[3], In1_t, In[0]);
  and and_28 (In6__In5__In4_In3_In2__In0, In6_t, In5_t, In[4], In[3], In2_t, In[0]);
  and and_29 (In5_In4_In3__In2__In1__In0, In[5], In[4], In3_t, In2_t, In1_t, In0_t);
  and and_30 (In6_In4_In3__In2__In1__In0, In[6], In[4], In3_t, In2_t, In1_t, In0_t);
  and and_31 (In6__In5__In4_In2__In1__In0, In6_t, In5_t, In[4], In2_t, In1_t, In[0]);
  and and_32 (In6__In5__In4_In3_In2__In1, In6_t, In5_t, In[4], In[3], In2_t, In1_t);
  and and_33 (In6_In5__In3_In2_In1__In0, In[6], In5_t, In[3], In[2], In1_t, In0_t);
  and and_34 (In6__In5_In3_In2__In1_In0, In6_t, In[5], In[3], In2_t, In[1], In0_t);
  and and_35 (In6__In5_In3__In2_In1__In0, In6_t, In[5], In3_t, In[2], In1_t, In[0]);
  and and_36 (In6_In5__In3__In2__In1_In0, In[6], In5_t, In3_t, In2_t, In[1], In[0]);
  and and_37 (In6_In5_In4_In2__In1__In0, In[6], In[5], In[4], In2_t, In1_t, In0_t);
  and and_38 (In6_In5_In4_In3__In2__In1, In[6], In[5], In[4], In3_t, In2_t, In1_t);
  and and_39 (In5__In4_In3_In2__In1__In0, In5_t, In[4], In[3], In2_t, In1_t, In[0]);
  and and_40 (In6__In4_In3_In2__In1__In0, In6_t, In[4], In[3], In2_t, In1_t, In[0]);
  and and_41 (In6_In5_In3__In2_In1_In0, In[6], In[5], In3_t, In[2], In[1], In0_t);
  and and_42 (In6__In5__In3_In2_In1_In0, In6_t, In5_t, In[3], In[2], In[1], In[0]);
  and and_43 (In6_In5_In3__In2__In1__In0, In[6], In[5], In3_t, In2_t, In1_t, In0_t);
  and and_44 (In6__In5__In3_In2__In1__In0, In6_t, In5_t, In[3], In2_t, In1_t, In[0]);
  and and_45 (In6_In5_In3_In2__In1__In0, In[6], In[5], In[3], In2_t, In1_t, In[0]);
  and and_46 (In6_In4__In2_In0, In[6], In4_t, In[2], In0_t);
  and and_47 (In5_In4__In3__In2, In[5], In4_t, In3_t, In[2]);
  and and_48 (In5__In4__In3_In2, In5_t, In4_t, In[3], In[2]);
  and and_49 (In6_In4__In3__In1, In[6], In4_t, In3_t, In[1]);
  and and_50 (In5_In4__In1_In0, In[5], In4_t, In[1], In0_t);
  and and_51 (In6__In4__In3_In1, In6_t, In4_t, In[3], In[1]);
  and and_52 (In6__In4__In2_In0, In6_t, In4_t, In[2], In[0]);
  and and_53 (In5__In4__In1_In0, In5_t, In4_t, In[1], In[0]);
  and and_54 (In6_In4__In3_In1, In[6], In4_t, In[3], In1_t);
  and and_55 (In5_In4__In3_In2, In[5], In4_t, In[3], In2_t);
  and and_56 (In6_In4__In2__In0, In[6], In4_t, In2_t, In[0]);
  and and_57 (In5_In4__In1__In0, In[5], In4_t, In1_t, In[0]);
  or or_1 (Output[6], In5_In4__In3__In2_In1_In0, In5__In4__In3_In2_In1__In0, In5__In4__In3__In2__In1_In0, In5_In4__In3_In2__In1__In0, In6_In5_In4_In3__In1__In0, In6_In5_In4_In3__In2__In0, In5_In4_In3__In2__In1__In0, In6_In4_In3__In2__In1__In0, In6_In5__In3_In2_In1__In0, In6_In5__In3__In2__In1_In0, In6_In5_In4_In2__In1__In0, In6_In5_In4_In3__In2__In1, In6_In5_In3__In2_In1_In0, In6_In5_In3__In2__In1__In0, In6_In5_In3_In2__In1__In0, In6_In4__In2_In0, In6_In4__In3__In1, In6_In4__In3_In1, In6_In4__In2__In0);
  or or_2 (Output[5], In6_In4__In3__In2_In1_In0, In6__In4__In3_In2__In1_In0, In6__In4__In3__In2_In1__In0, In6_In4__In3_In2__In1__In0, In6_In5_In4_In3__In1__In0, In6_In5_In4_In3__In2__In0, In5_In4_In3__In2__In1__In0, In6_In4_In3__In2__In1__In0, In6__In5_In3_In2__In1_In0, In6__In5_In3__In2_In1__In0, In6_In5_In4_In2__In1__In0, In6_In5_In4_In3__In2__In1, In6_In5_In3__In2_In1_In0, In6_In5_In3__In2__In1__In0, In6_In5_In3_In2__In1__In0, In5_In4__In3__In2, In5_In4__In1_In0, In5_In4__In3_In2, In5_In4__In1__In0);
  or or_3 (Output[4], In6_In5_In4_In3__In1__In0, In6_In5_In4_In3__In2__In0, In6__In5__In4_In3_In1__In0, In6__In5__In4_In3_In2__In0, In5_In4_In3__In2__In1__In0, In6_In4_In3__In2__In1__In0, In6__In5__In4_In2__In1__In0, In6__In5__In4_In3_In2__In1, In6_In5_In4_In2__In1__In0, In6_In5_In4_In3__In2__In1, In5__In4_In3_In2__In1__In0, In6__In4_In3_In2__In1__In0, In6_In5_In3__In2__In1__In0, In6__In5__In3_In2__In1__In0);
  or or_4 (Output[3], In6__In5__In4__In2_In1_In0, In6_In5__In4__In2_In1__In0, In6__In5_In4__In2__In1_In0, In6_In5_In4__In2__In1__In0, In6__In5__In4_In3_In1__In0, In6__In5__In4_In3_In2__In0, In6__In5__In4_In2__In1__In0, In6__In5__In4_In3_In2__In1, In6_In5__In3_In2_In1__In0, In6__In5_In3_In2__In1_In0, In5__In4_In3_In2__In1__In0, In6__In4_In3_In2__In1__In0, In6__In5__In3_In2_In1_In0, In6__In5__In3_In2__In1__In0, In6_In5_In3_In2__In1__In0, In5__In4__In3_In2, In6__In4__In3_In1, In6_In4__In3_In1, In5_In4__In3_In2);
  or or_5 (Output[2], In6_In5_In4__In3__In1_In0, In6__In5__In4__In3_In1_In0, In6_In5__In4__In3_In1__In0, In6__In5_In4__In3__In1__In0, In6_In5__In3_In2_In1__In0, In6__In5_In3__In2_In1__In0, In6_In5_In3__In2_In1_In0, In6__In5__In3_In2_In1_In0, In6_In4__In2_In0, In5_In4__In3__In2, In5__In4__In3_In2, In6__In4__In2_In0);
  or or_6 (Output[1], In6_In5_In4__In3__In2_In0, In6__In5__In4__In3_In2_In0, In6__In5_In4__In3_In2__In0, In6_In5__In4__In3__In2__In0, In6__In5_In3_In2__In1_In0, In6_In5__In3__In2__In1_In0, In6_In5_In3__In2_In1_In0, In6__In5__In3_In2_In1_In0, In6_In4__In3__In1, In5_In4__In1_In0, In6__In4__In3_In1, In5__In4__In1_In0);
  or or_7 (Output[0], In6__In5__In4__In3_In2_In1, In6__In5_In4__In3__In2_In1, In6_In5__In4__In3__In2__In1, In6_In5_In4__In3_In2__In1, In6__In5__In4_In3_In1__In0, In6__In5__In4_In3_In2__In0, In6__In5__In4_In2__In1__In0, In6__In5__In4_In3_In2__In1, In6__In5_In3__In2_In1__In0, In6_In5__In3__In2__In1_In0, In5__In4_In3_In2__In1__In0, In6__In4_In3_In2__In1__In0, In6__In5__In3_In2_In1_In0, In6__In5__In3_In2__In1__In0, In6_In5_In3_In2__In1__In0, In6__In4__In2_In0, In5__In4__In1_In0, In6_In4__In2__In0, In5_In4__In1__In0);

  // Other names for the same wires on the sheet: O0 = Output[0]; O1 = Output[1]; O2 = Output[2]; O3 = Output[3];
  //   O4 = Output[4]; O5 = Output[5]; O6 = Output[6]
endmodule
