// Digital circuit Template.dig as structural Verilog
module Template (
  input  A,
  input  B,
  input  C,
  input  D,
  output After,
  output [4:0] CheckGlitch,
  output Before
);

  wire and_1_out, and_2_out, and_3_out, and_4_out, not_1_out, not_2_out, not_3_out;

  not not_1 (not_1_out, A);
  not not_2 (not_2_out, C);
  not not_3 (not_3_out, B);
  and and_1 (and_1_out, D, not_2_out);
  and and_2 (and_2_out, not_3_out, D);
  and and_3 (and_3_out, ~C, D);  // And
  and and_4 (and_4_out, A, ~B, D);  // And
  or or_1 (After, not_1_out, and_1_out, and_2_out);
  or or_2 (Before, ~A, and_3_out, and_4_out);  // Or
  Counter #(.Bits(5)) counter_1 (.en(1'b1), .C(After), .clr(1'b0), .out(CheckGlitch));  // open: ovf

  // Notes on the sheet:
  //   Must not change this section
endmodule

/* Test case T1:
A B C D Before After CheckGlitch
0 0 0 0 1 1 1
0 0 0 1 1 1 1
0 0 1 1 1 1 1
1 0 1 1 1 1 1
0 0 1 1 1 1 1
1 0 1 1 1 1 1
0 0 1 1 1 1 1
*/
