// Digital circuit Lab05_05.dig as structural Verilog
module Lab05_05 (
  input  T,
  input  Clock,
  input  Clear,
  output Q,
  output Q_2
);

  wire and_1_out, nor_1_out, nor_2_out, nor_3_out, nor_4_out, nor_5_out, nor_6_out, not_1_out;

  and and_1 (and_1_out, Q, T);
  nor nor_1 (nor_1_out, T, Q);
  not not_1 (not_1_out, Clock);
  nor nor_2 (nor_2_out, and_1_out, nor_1_out, Clear);
  nor nor_3 (nor_3_out, nor_6_out, nor_4_out);
  nor nor_4 (nor_4_out, nor_3_out, not_1_out);
  nor nor_5 (nor_5_out, nor_4_out, not_1_out, nor_6_out);
  nor nor_6 (nor_6_out, nor_5_out, nor_2_out);
  nor nor_7 (Q, nor_4_out, Q_2);
  nor nor_8 (Q_2, Q, nor_5_out);
endmodule
