// Digital circuit binary-encode-excess3.dig as structural Verilog
module binary_encode_excess3 (
  input  i1,
  input  i2,
  input  i3,
  input  i4,
  output E1,
  output E2,
  output E3,
  output E4
);

  wire not_1_out, not_2_out, not_3_out, not_4_out, not_5_out, not_6_out, not_7_out, not_8_out, not_9_out,
       not_10_out, not_11_out, not_12_out, not_13_out, not_14_out, not_15_out, not_16_out, not_17_out, P1,
       P2, P3, P4, P5, P6, P7, P8, P9;

  not not_1 (not_1_out, i1);
  not not_2 (not_2_out, i2);
  not not_3 (not_3_out, i3);
  not not_4 (not_4_out, i2);
  not not_5 (not_5_out, i3);
  not not_6 (not_6_out, i1);
  not not_7 (not_7_out, i3);
  not not_8 (not_8_out, i4);
  not not_9 (not_9_out, i1);
  not not_10 (not_10_out, i1);
  not not_11 (not_11_out, i1);
  not not_12 (not_12_out, i2);
  not not_13 (not_13_out, i2);
  not not_14 (not_14_out, i3);
  not not_15 (not_15_out, i4);
  not not_16 (not_16_out, i1);
  not not_17 (not_17_out, i4);
  and and_1 (P1, not_1_out, i2, i3);
  and and_2 (P2, i1, not_2_out, not_3_out);
  and and_3 (P3, not_4_out, not_5_out, i4);
  and and_4 (P4, not_6_out, i2, not_7_out, not_8_out);
  and and_5 (P5, not_9_out, i2, i4);
  and and_6 (P6, not_10_out, i3, i4);
  and and_7 (P7, not_11_out, not_12_out, i3);
  and and_8 (P8, not_13_out, not_14_out, not_15_out);
  and and_9 (P9, not_16_out, not_17_out);
  or or_1 (E1, P1, P2, P5);
  or or_2 (E2, P3, P4, P7);
  or or_3 (E3, P4, P6, P8);
  or or_4 (E4, P8, P9);

  // Other names for the same wires on the sheet: out_E1 = E1; out_E2 = E2; out_E3 = E3; out_E4 = E4
endmodule

/* Test case binary-encode-excess3:
i1 i2 i3 i4 E1 E2 E3 E4
0 0 0 0 0 0 1 1
0 0 0 1 0 1 0 0
0 0 1 0 0 1 0 1
0 0 1 1 0 1 1 0
0 1 0 0 0 1 1 1
0 1 0 1 1 0 0 0
0 1 1 0 1 0 0 1
0 1 1 1 1 0 1 0
1 0 0 0 1 0 1 1
1 0 0 1 1 1 0 0
1 0 1 0 0 0 0 0
1 0 1 1 0 0 0 0
1 1 0 0 0 0 0 0
1 1 0 1 0 0 0 0
1 1 1 0 0 0 0 0
1 1 1 1 0 0 0 0
*/
